# Fritzing sketch fritzing colorsortbot (saved by Fritzing 0.9.3b)

parts:
  Composant1 = Arduino Uno (Rev3)
  J1 = Basic Servo  # not connected
  J3 = Basic Servo  # not connected
  J4 = Basic Servo  # not connected
  J5 = Basic Servo  # not connected
  J6 = Basic Servo  # not connected
  PWM1 = PCA9685 16x12-bit PWM Breakout
  U1 = LIPO-2000mAh [package=lipo-2000]  # not connected
  J7 = Basic Servo  # not connected

nets:
  N1: Composant1.A4/SDA, PWM1.no_name_yet#604
  N2: Composant1.A5/SCL, PWM1.no_name_yet#603
  N3: Composant1.5V, PWM1.no_name_yet#602
  N4: Composant1.GND, PWM1.no_name_yet#601
